// Logisim project BeyzaKoser_1521221046.circ as structural Verilog: 1 circuit, main circuit org_odev2
// BeyzaKoser
module org_odev2 (
  input  dWrite,
  input  in_2,
  input  [7:0] Write_Data,
  input  in_4,
  input  in_5,
  input  [1:0] in_6,
  input  in_7,
  input  [1:0] in_8,
  input  [1:0] in_9,
  input  [1:0] in_10,
  output [7:0] out_11,
  output [7:0] data,
  output [7:0] out_13,
  output [7:0] store_Data,
  output [1:0] opcode,
  output [7:0] out_16,
  output [1:0] Rhedef,
  output [7:0] out_18,
  output [1:0] Rkaynak1,
  output [1:0] Rkaynak2
);

  wire clock_1_out, clock_2_out, clock_3_out, demultiplexer_1_out0, demultiplexer_1_out1,
       demultiplexer_1_out2, demultiplexer_1_out3;
  wire [7:0] adder_2_out, PC_q, register_1_q, register_2_q, register_3_q, register_4_q, subtractor_1_out;

  Clock clock_1 (.out(clock_1_out));
  Register PC (.D(out_11), .en(in_2), .Q(PC_q), .clk(clock_1_out), .clr(in_4));
  Adder adder_1 (.a(8'h1), .b(PC_q), .out(out_11));  // open: cin, cout
  ROM rom_1 (.addr(PC_q), .data(out_18), .sel(in_5));
  Demultiplexer #(.select(2), .enable("false")) demultiplexer_1 (
    .out0(demultiplexer_1_out0), .out1(demultiplexer_1_out1), .out2(demultiplexer_1_out2),
    .out3(demultiplexer_1_out3), .in(dWrite), .sel(Rkaynak1));
  BitSelector #(.group(2)) bitselector_1 (.in(out_18), .out(opcode), .sel(in_6));
  BitSelector #(.group(2)) bitselector_2 (.in(out_18), .out(Rhedef), .sel(in_8));
  BitSelector #(.group(2)) bitselector_3 (.in(out_18), .out(Rkaynak1), .sel(in_9));
  BitSelector #(.group(2)) bitselector_4 (.in(out_18), .out(Rkaynak2), .sel(in_10));
  Clock clock_2 (.out(clock_2_out));
  Register register_1 (.D(Write_Data), .en(demultiplexer_1_out0), .Q(register_1_q), .clk(clock_2_out));  // open: clr
  Register register_2 (.D(Write_Data), .en(demultiplexer_1_out1), .Q(register_2_q), .clk(clock_2_out));  // open: clr
  Register register_3 (.D(Write_Data), .en(demultiplexer_1_out2), .Q(register_3_q), .clk(clock_2_out));  // open: clr
  Register register_4 (.D(Write_Data), .en(demultiplexer_1_out3), .Q(register_4_q), .clk(clock_2_out));  // open: clr
  Multiplexer #(.select(2), .width(8), .enable("false")) multiplexer_1 (
    .in0(register_1_q), .in1(register_2_q), .in2(register_3_q), .in3(register_4_q), .out(out_13),
    .sel(Rkaynak1));
  Multiplexer #(.select(2), .width(8), .enable("false")) multiplexer_2 (
    .in0(register_1_q), .in1(register_2_q), .in2(register_3_q), .in3(register_4_q), .out(out_16),
    .sel(Rkaynak2));
  Adder adder_2 (.a(out_13), .b(out_16), .out(adder_2_out));  // open: cin, cout
  Subtractor subtractor_1 (.a(out_13), .b(out_16), .out(subtractor_1_out));  // open: bin, bout
  Multiplexer #(.select(2), .width(8), .enable("false")) multiplexer_3 (
    .in0(adder_2_out), .in1(subtractor_1_out), .out(data), .sel(opcode));  // open: in2, in3
  RAM #(.addrWidth(2), .bus("separate")) ram_1 (
    .addr(Rhedef), .din(data), .data(store_Data), .str(in_7), .clk(clock_3_out));  // open: sel, ld, clr
  Clock clock_3 (.out(clock_3_out));

  // Other names for the same wires on the sheet: drs[1:0] = Rkaynak1

  // Notes on the sheet:
  //   program counter
  //   instruction memory
  //   contents of rom_1 (hex, n*v repeats v):
  //   1 10 27 28 1 2 28 11 22 4 1 10 28 3 12 14
  //   Register file
  //   r0
  //   r1
  //   r2
  //   r3
  //   rt
  //   rs
  //   Alu
  //   00=toplama
  //   01=çıkarma
  //   Memory
endmodule
